// Logisim project Examen_1erParcial_JFGR.circ as structural Verilog: 8 circuits, main circuit Sumador
module Principal (
  input  in_1,
  input  in_2,
  input  A,
  input  in_4,
  input  in_5,
  input  in_6,
  input  B,
  input  in_8,
  input  in_9,
  input  in_10,
  output out_11,
  output out_12,
  output Salida,
  output out_14,
  output out_15
);

  wire and_1_out_9, and_1_out_10, and_1_out_12, and_1_out_13, and_1_salida, demultiplexor_1_out_3,
       demultiplexor_1_out_5, demultiplexor_1_out_6, demultiplexor_1_salida, multiand_1_out_7,
       multiand_1_out_8, multiand_1_out_10, multiand_1_out_11, multiand_1_salida, multiand_2_out_7,
       multiand_2_out_8, multiand_2_out_10, multiand_2_out_11, multiand_2_salida, multiand_3_out_7,
       multiand_3_out_8, multiand_3_out_10, multiand_3_out_11, multiand_3_salida, multiand_4_out_7,
       multiand_4_out_8, multiand_4_out_10, multiand_4_out_11, multiand_4_salida, or_1_out_9, or_1_out_10,
       or_1_out_12, or_1_out_13, or_1_salida, restador_1_out_9, restador_1_out_10, restador_1_out_12,
       restador_1_out_13, restador_1_salida, sumador_1_out_9, sumador_1_out_10, sumador_1_out_12,
       sumador_1_out_13, sumador_1_salida;

  Demultiplexor demultiplexor_1 (
    .BA(in_1), .in_2(in_2), .out_3(demultiplexor_1_out_3), .Salida(demultiplexor_1_salida),
    .out_5(demultiplexor_1_out_5), .out_6(demultiplexor_1_out_6));
  Sumador sumador_1 (
    .A(A), .in_2(in_4), .in_3(in_5), .in_4(in_6), .B(B), .in_6(in_8), .in_7(in_9), .in_8(in_10),
    .out_9(sumador_1_out_9), .out_10(sumador_1_out_10), .Salida(sumador_1_salida), .out_12(sumador_1_out_12),
    .out_13(sumador_1_out_13));
  MultiAnd multiand_1 (
    .in_3(sumador_1_out_10), .in_4(sumador_1_salida), .out_7(multiand_1_out_7), .out_8(multiand_1_out_8),
    .Salida(multiand_1_salida), .out_10(multiand_1_out_10), .in_5(sumador_1_out_12), .in_6(sumador_1_out_13),
    .in_1(demultiplexor_1_out_6), .in_2(sumador_1_out_9), .out_11(multiand_1_out_11));
  Restador restador_1 (
    .A(A), .in_2(in_4), .in_3(in_5), .in_4(in_6), .B(B), .in_6(in_8), .in_7(in_9), .in_8(in_10),
    .out_9(restador_1_out_9), .out_10(restador_1_out_10), .Salida(restador_1_salida),
    .out_12(restador_1_out_12), .out_13(restador_1_out_13));
  MultiAnd multiand_2 (
    .in_3(restador_1_out_10), .in_4(restador_1_salida), .out_7(multiand_2_out_7), .out_8(multiand_2_out_8),
    .Salida(multiand_2_salida), .out_10(multiand_2_out_10), .in_5(restador_1_out_12),
    .in_6(restador_1_out_13), .in_1(demultiplexor_1_out_5), .in_2(restador_1_out_9),
    .out_11(multiand_2_out_11));
  MultiOr multior_1 (
    .in_1(multiand_1_out_7), .in_2(multiand_1_out_8), .in_3(multiand_1_salida), .in_4(multiand_1_out_10),
    .in_5(multiand_1_out_11), .in_6(multiand_2_out_7), .in_7(multiand_2_out_8), .in_8(multiand_2_salida),
    .in_9(multiand_2_out_10), .in_10(multiand_2_out_11), .in_11(multiand_3_out_7), .in_12(multiand_3_out_8),
    .in_13(multiand_3_salida), .in_14(multiand_3_out_10), .in_15(multiand_3_out_11),
    .in_16(multiand_4_out_7), .in_17(multiand_4_out_8), .in_18(multiand_4_salida), .in_19(multiand_4_out_10),
    .in_20(multiand_4_out_11), .out_21(out_11), .out_22(out_12), .Salida(Salida), .out_24(out_14),
    .out_25(out_15));
  Or or_1 (
    .A(A), .in_2(in_4), .in_3(in_5), .in_4(in_6), .B(B), .in_6(in_8), .in_7(in_9), .in_8(in_10),
    .out_9(or_1_out_9), .out_10(or_1_out_10), .Salida(or_1_salida), .out_12(or_1_out_12), .out_13(or_1_out_13));
  MultiAnd multiand_3 (
    .in_3(or_1_out_10), .in_4(or_1_salida), .out_7(multiand_3_out_7), .out_8(multiand_3_out_8),
    .Salida(multiand_3_salida), .out_10(multiand_3_out_10), .in_5(or_1_out_12), .in_6(or_1_out_13),
    .in_1(demultiplexor_1_salida), .in_2(or_1_out_9), .out_11(multiand_3_out_11));
  And and_1 (
    .A(A), .in_2(in_4), .in_3(in_5), .in_4(in_6), .B(B), .in_6(in_8), .in_7(in_9), .in_8(in_10),
    .out_9(and_1_out_9), .out_10(and_1_out_10), .Salida(and_1_salida), .out_12(and_1_out_12),
    .out_13(and_1_out_13));
  MultiAnd multiand_4 (
    .in_3(and_1_out_10), .in_4(and_1_salida), .out_7(multiand_4_out_7), .out_8(multiand_4_out_8),
    .Salida(multiand_4_salida), .out_10(multiand_4_out_10), .in_5(and_1_out_12), .in_6(and_1_out_13),
    .in_1(demultiplexor_1_out_3), .in_2(and_1_out_9), .out_11(multiand_4_out_11));

  // Notes on the sheet:
  //   EXAMEN 1er PARCIAL
  //   Juan Francisco Gallo Ramírez
  //   ___________________________________________________________
  //   Entrada
  //   Entrada
endmodule

module Sumador (
  input  A,
  input  in_2,
  input  in_3,
  input  in_4,
  input  B,
  input  in_6,
  input  in_7,
  input  in_8,
  output out_9,
  output out_10,
  output Salida,
  output out_12,
  output out_13
);

  wire and_1_out, and_2_out, and_3_out, and_4_out, and_5_out, and_6_out, and_7_out, and_8_out, or_2_out,
       or_3_out, or_4_out, xor_1_out, xor_3_out, xor_5_out, xor_7_out;

  and and_1 (and_1_out, A, B);
  and and_2 (and_2_out, or_2_out, xor_1_out);
  or or_1 (out_9, and_1_out, and_2_out);
  xor xor_1 (xor_1_out, A, B);
  xor xor_2 (out_10, or_2_out, xor_1_out);
  and and_3 (and_3_out, in_2, in_6);
  and and_4 (and_4_out, or_3_out, xor_3_out);
  or or_2 (or_2_out, and_3_out, and_4_out);
  xor xor_3 (xor_3_out, in_2, in_6);
  xor xor_4 (Salida, or_3_out, xor_3_out);
  and and_5 (and_5_out, in_3, in_7);
  and and_6 (and_6_out, or_4_out, xor_5_out);
  or or_3 (or_3_out, and_5_out, and_6_out);
  xor xor_5 (xor_5_out, in_3, in_7);
  xor xor_6 (out_12, or_4_out, xor_5_out);
  and and_7 (and_7_out, in_4, in_8);
  and and_8 (and_8_out, 1'b0, xor_7_out);
  or or_4 (or_4_out, and_7_out, and_8_out);
  xor xor_7 (xor_7_out, in_4, in_8);
  xor xor_8 (out_13, 1'b0, xor_7_out);

  // Notes on the sheet:
  //   SUMADOR
  //   4 bits
  //   _____________________________________________
  //   Entrada
  //   Entrada
endmodule

module Restador (
  input  A,
  input  in_2,
  input  in_3,
  input  in_4,
  input  B,
  input  in_6,
  input  in_7,
  input  in_8,
  output out_9,
  output out_10,
  output Salida,
  output out_12,
  output out_13
);

  wire not_1_out, not_2_out, not_3_out, not_4_out, sumador_1_out_9, sumador_2_out_9, sumador_2_out_10,
       sumador_2_out_12, sumador_2_out_13, sumador_2_salida;

  Sumador sumador_1 (
    .A(A), .in_2(in_2), .in_3(in_3), .in_4(in_4), .B(sumador_2_out_10), .in_6(sumador_2_salida),
    .in_7(sumador_2_out_12), .in_8(sumador_2_out_13), .out_9(sumador_1_out_9), .out_10(out_10),
    .Salida(Salida), .out_12(out_12), .out_13(out_13));
  xor xor_1 (out_9, sumador_2_out_9, ~sumador_1_out_9);  // XOR_Gate
  not not_1 (not_1_out, in_7);
  not not_2 (not_2_out, in_6);
  not not_3 (not_3_out, B);
  not not_4 (not_4_out, in_8);
  Sumador sumador_2 (
    .A(not_3_out), .in_2(not_2_out), .in_3(not_1_out), .in_4(not_4_out), .B(1'b0), .in_6(1'b0), .in_7(1'b0),
    .in_8(1'b1), .out_9(sumador_2_out_9), .out_10(sumador_2_out_10), .Salida(sumador_2_salida),
    .out_12(sumador_2_out_12), .out_13(sumador_2_out_13));

  // Notes on the sheet:
  //   RESTADOR
  //   4 bits
  //   _____________________________________________
  //   Entrada
  //   Entrada
endmodule

module Or (
  input  A,
  input  in_2,
  input  in_3,
  input  in_4,
  input  B,
  input  in_6,
  input  in_7,
  input  in_8,
  output out_9,
  output out_10,
  output Salida,
  output out_12,
  output out_13
);

  or or_1 (out_10, A, B);
  or or_2 (Salida, in_2, in_6);
  or or_3 (out_12, in_3, in_7);
  or or_4 (out_13, in_4, in_8);

  assign out_9 = 1'b0;

  // Notes on the sheet:
  //   OPERACIÓN OR
  //   4 bits
  //   _____________________________________________
  //   Entrada
  //   Entrada
endmodule

module And (
  input  A,
  input  in_2,
  input  in_3,
  input  in_4,
  input  B,
  input  in_6,
  input  in_7,
  input  in_8,
  output out_9,
  output out_10,
  output Salida,
  output out_12,
  output out_13
);

  and and_1 (out_10, A, B);
  and and_2 (Salida, in_2, in_6);
  and and_3 (out_13, in_4, in_8);
  and and_4 (out_12, in_3, in_7);

  assign out_9 = 1'b0;

  // Notes on the sheet:
  //   OPERACIÓN AND
  //   4 bits
  //   _____________________________________________
  //   Entrada
  //   Entrada
endmodule

module Demultiplexor (
  input  BA,
  input  in_2,
  output out_3,
  output Salida,
  output out_5,
  output out_6
);

  wire not_1_out, not_2_out;

  and and_1 (out_3, BA, in_2);
  and and_2 (Salida, BA, not_2_out);
  not not_1 (not_1_out, BA);
  and and_3 (out_5, not_1_out, in_2);
  and and_4 (out_6, not_1_out, not_2_out);
  not not_2 (not_2_out, in_2);

  // Notes on the sheet:
  //   DEMULTIPLEXOR
  //   2 a 4 bits
  //   _____________________________________________
  //   Entrada
endmodule

module MultiAnd (
  input  in_1,
  input  in_2,
  input  in_3,
  input  in_4,
  input  in_5,
  input  in_6,
  output out_7,
  output out_8,
  output Salida,
  output out_10,
  output out_11
);

  and and_1 (out_7, in_1, in_2);
  and and_2 (Salida, in_1, in_4);
  and and_3 (out_8, in_1, in_3);
  and and_4 (out_10, in_1, in_5);
  and and_5 (out_11, in_1, in_6);

  // Notes on the sheet:
  //   MULTICOMPUERTA AND
  //   6 bits entrada - 5 bits salida
  //   _____________________________________________
  //   Entrada
endmodule

module MultiOr (
  input  in_1,
  input  in_2,
  input  in_3,
  input  in_4,
  input  in_5,
  input  in_6,
  input  in_7,
  input  in_8,
  input  in_9,
  input  in_10,
  input  in_11,
  input  in_12,
  input  in_13,
  input  in_14,
  input  in_15,
  input  in_16,
  input  in_17,
  input  in_18,
  input  in_19,
  input  in_20,
  output out_21,
  output out_22,
  output Salida,
  output out_24,
  output out_25
);

  or or_1 (out_21, in_1, in_6, in_11, in_16);
  or or_2 (Salida, in_3, in_8, in_13, in_18);
  or or_3 (out_22, in_2, in_7, in_12, in_17);
  or or_4 (out_24, in_4, in_9, in_14, in_19);
  or or_5 (out_25, in_5, in_10, in_15, in_20);

  // Notes on the sheet:
  //   MULTICOMPUERTA OR
  //   20 bits entrada - 5 bits salida
  //   _____________________________________________
  //   Entrada
endmodule
